# Fritzing sketch tinytx_rht03_breakout (saved by Fritzing 0.9.2b)
stripboards: 1

parts:
  J1 = female pin header, 8 pins [form="♀ (female)"]
  J2 = female pin header, 4 pins [form="♀ (female)"]
  R1 = Resistor [tolerance=±5% resistance=1k package=THT]

nets:
  N1: J1.pin1, J2.pin3
  N2: J1.pin3, J2.pin4
  N3: J1.pin5, R1.Pin_1
  N4: J1.pin6, R1.Pin_0
  N5: J1.pin7, J2.pin1, J2.pin2

notes:
  PWR (10)
  SIG (9)
  Gnd
